// Logisim project sort.circ as structural Verilog: 3 circuits, main circuit main
module main (
  input  [7:0] x0,
  input  [7:0] x0_2,
  input  [1:0] sel0,
  input  [1:0] sel0_2,
  input  en0,
  input  en0_2,
  input  [1:0] sela,
  input  [1:0] sela_2,
  input  [7:0] x1,
  input  [7:0] x1_2,
  input  [1:0] sel1,
  input  [1:0] sel1_2,
  input  en1,
  input  en1_2,
  input  [1:0] selb,
  input  [1:0] selb_2,
  input  [7:0] x2,
  input  [7:0] x2_2,
  input  [1:0] sel2,
  input  [1:0] sel2_2,
  input  en2,
  input  en2_2,
  input  [1:0] selc,
  input  [7:0] x3,
  input  [7:0] x3_2,
  input  [1:0] sel3,
  input  [1:0] sel3_2,
  input  en3,
  input  en3_2,
  input  [1:0] seld,
  input  rst,
  input  rst_2,
  input  cf,
  input  cf0,
  input  rst_3,
  input  cf1,
  input  flag,
  input  rst_4,
  input  flag0,
  input  flag1,
  input  opr,
  output cf0_2,
  output cf0_3,
  output flag0_2,
  output flag_2,
  output cf1_2,
  output flag1_2
);

  wire clk_2_out, clk_out;
  wire [7:0] multiplexer_1_out, multiplexer_2_out, multiplexer_3_out, multiplexer_4_out, multiplexer_5_out,
       multiplexer_6_out, multiplexer_7_out, multiplexer_8_out, multiplexer_9_out, multiplexer_10_out,
       multiplexer_11_out, multiplexer_12_out, multiplexer_13_out, multiplexer_14_out, r0_s0_2_q, r0_s0_q,
       r1_s1_2_q, r1_s1_q, r2_s2_2_q, r2_s2_q, r3_s3_2_q, r3_s3_q;

  Control_Unit control_unit_1 ();  // open: cf, rst, en0, en1, en2, en3, sel0, sel1, sel2, sel3, sela, selb, done, flag
  Clock clk (.out(clk_out));
  Multiplexer #(.select(2), .width(8), .enable("false")) multiplexer_1 (
    .in0(x0), .in1(multiplexer_2_out), .in2(multiplexer_3_out), .in3(multiplexer_4_out),
    .out(multiplexer_1_out), .sel(sel0));
  Multiplexer #(.select(2), .width(8), .enable("false")) multiplexer_2 (
    .in0(multiplexer_1_out), .in1(x1), .in2(multiplexer_3_out), .in3(multiplexer_4_out),
    .out(multiplexer_2_out), .sel(sel1));
  Multiplexer #(.select(2), .width(8), .enable("false")) multiplexer_3 (
    .in0(multiplexer_1_out), .in1(multiplexer_2_out), .in2(x2), .in3(multiplexer_4_out),
    .out(multiplexer_3_out), .sel(sel2));
  Multiplexer #(.select(2), .width(8), .enable("false")) multiplexer_4 (
    .in0(multiplexer_1_out), .in1(multiplexer_2_out), .in2(multiplexer_3_out), .in3(x3),
    .out(multiplexer_4_out), .sel(sel3));
  Register r0_s0 (.D(multiplexer_1_out), .en(clk_out), .Q(r0_s0_q), .clk(en0), .clr(rst));
  Register r1_s1 (.D(multiplexer_2_out), .en(clk_out), .Q(r1_s1_q), .clk(en1), .clr(rst));
  Register r2_s2 (.D(multiplexer_3_out), .en(clk_out), .Q(r2_s2_q), .clk(en2), .clr(rst));
  Register r3_s3 (.D(multiplexer_4_out), .en(clk_out), .Q(r3_s3_q), .clk(en3), .clr(rst));
  Control_Unit control_unit_2 (
    .cf(cf), .rst(rst_3), .flag(flag));  // open: en0, en1, en2, en3, sel0, sel1, sel2, sel3, sela, selb, done
  Multiplexer #(.select(2), .width(8), .enable("false")) multiplexer_5 (
    .in0(r0_s0_q), .in1(r1_s1_q), .in2(r2_s2_q), .in3(r3_s3_q), .out(multiplexer_5_out), .sel(sela));
  Multiplexer #(.select(2), .width(8), .enable("false")) multiplexer_6 (
    .in0(r0_s0_q), .in1(r1_s1_q), .in2(r2_s2_q), .in3(r3_s3_q), .out(multiplexer_6_out), .sel(selb));
  Multiplexer #(.select(2), .width(8), .enable("false")) multiplexer_7 (
    .in0(r0_s0_q), .in1(r1_s1_q), .in2(r2_s2_q), .in3(r3_s3_q), .out(multiplexer_7_out), .sel(selc));
  Multiplexer #(.select(2), .width(8), .enable("false")) multiplexer_8 (
    .in0(r0_s0_q), .in1(r1_s1_q), .in2(r2_s2_q), .in3(r3_s3_q), .out(multiplexer_8_out), .sel(seld));
  xor xor_1 (flag0_2, multiplexer_5_out[7], multiplexer_6_out[7]);
  xor xor_2 (flag1_2, multiplexer_7_out[7], multiplexer_8_out[7]);
  Subtractor subtractor_1 (.a(multiplexer_5_out), .b(multiplexer_6_out), .bout(cf0_2));  // open: out, bin
  Subtractor subtractor_2 (.a(multiplexer_7_out), .b(multiplexer_8_out), .bout(cf1_2));  // open: out, bin
  cu cu_1 (
    .in_1(cf0), .cf(cf1), .rst(rst_4), .flag(flag0), .in_5(flag1), .opr(opr));  // open: en0, en1, en2, en3, sel0, sel1, sel2, sel3, sela, selb, done
  Multiplexer #(.select(2), .width(8), .enable("false")) multiplexer_9 (
    .in0(x0_2), .in1(multiplexer_10_out), .in2(multiplexer_11_out), .in3(multiplexer_12_out),
    .out(multiplexer_9_out), .sel(sel0_2));
  Multiplexer #(.select(2), .width(8), .enable("false")) multiplexer_10 (
    .in0(multiplexer_9_out), .in1(x1_2), .in2(multiplexer_11_out), .in3(multiplexer_12_out),
    .out(multiplexer_10_out), .sel(sel1_2));
  Multiplexer #(.select(2), .width(8), .enable("false")) multiplexer_11 (
    .in0(multiplexer_9_out), .in1(multiplexer_10_out), .in2(x2_2), .in3(multiplexer_12_out),
    .out(multiplexer_11_out), .sel(sel2_2));
  Multiplexer #(.select(2), .width(8), .enable("false")) multiplexer_12 (
    .in0(multiplexer_9_out), .in1(multiplexer_10_out), .in2(multiplexer_11_out), .in3(x3_2),
    .out(multiplexer_12_out), .sel(sel3_2));
  Clock clk_2 (.out(clk_2_out));
  Register r0_s0_2 (.D(multiplexer_9_out), .en(clk_2_out), .Q(r0_s0_2_q), .clk(en0_2), .clr(rst_2));
  Register r1_s1_2 (.D(multiplexer_10_out), .en(clk_2_out), .Q(r1_s1_2_q), .clk(en1_2), .clr(rst_2));
  Register r2_s2_2 (.D(multiplexer_11_out), .en(clk_2_out), .Q(r2_s2_2_q), .clk(en2_2), .clr(rst_2));
  Register r3_s3_2 (.D(multiplexer_12_out), .en(clk_2_out), .Q(r3_s3_2_q), .clk(en3_2), .clr(rst_2));
  Multiplexer #(.select(2), .width(8), .enable("false")) multiplexer_13 (
    .in0(r0_s0_2_q), .in1(r1_s1_2_q), .in2(r2_s2_2_q), .in3(r3_s3_2_q), .out(multiplexer_13_out), .sel(sela_2));
  Multiplexer #(.select(2), .width(8), .enable("false")) multiplexer_14 (
    .in0(r0_s0_2_q), .in1(r1_s1_2_q), .in2(r2_s2_2_q), .in3(r3_s3_2_q), .out(multiplexer_14_out), .sel(selb_2));
  xor xor_3 (flag_2, multiplexer_13_out[7], multiplexer_14_out[7]);
  Subtractor subtractor_3 (.a(multiplexer_13_out), .b(multiplexer_14_out), .bout(cf0_3));  // open: out, bin

  // Notes on the sheet:
  //   en0-3,sel0-3,sela,selb,done
  //   a
  //   b
  //   c
  //   d
  //   Control Unit (with opr)(with 2ALU)
  //   en0-3,sel0-3,sela-d,done
  //   a
  //   b
endmodule

module Control_Unit (
  input  cf,
  input  rst,
  input  flag,
  output en0,
  output en1,
  output en2,
  output en3,
  output sel0,
  output sel1,
  output sel2,
  output sel3,
  output sela,
  output selb,
  output done
);

  Clock clk ();  // open: out
endmodule

module cu (
  input  in_1,
  input  cf,
  input  rst,
  input  flag,
  input  in_5,
  input  opr,
  output en0,
  output en1,
  output en2,
  output en3,
  output sel0,
  output sel1,
  output sel2,
  output sel3,
  output sela,
  output selb,
  output done
);

  Clock clk ();  // open: out
endmodule
